# Fritzing sketch Space Invaders (saved by Fritzing 1.0.3b)
breadboards: 1

parts:
  Mod1 = Heltec WiFi LoRa 32 V2 [part_number=HTIT-WB32LA]
  S1 = Pushbutton [package="[SMD]"]
  U1 = POT [knob_status=50% power=0.5W package=alps_pot]
  S2 = JOYSTICK_MINI [package=joystick_mini]

nets:
  N1: Mod1.pin_10, S1.Pin_3, S1.Pin_4
  N2: Mod1.pin_11, U1.S
  N3: Mod1.pin_16, Mod1.pin_17, S1.Pin_1, S1.Pin_2, U1.E
  N4: Mod1.GND, U1.A
  N5: Mod1.pin_20, S2.LEFT
  N6: Mod1.pin_21, Mod1.pin_22
  N7: Mod1.pin_24, S2.GND
  N8: Mod1.pin_25, S2.DOWN
  N9: Mod1.pin_26, S2.CENT
